# Fritzing sketch ArduinoMini_Photogate_Receiver (saved by Fritzing 0.9.3b)
circuit board: 10.0199cm x 6.02576cm
stripboards: 1
breadboards: 1

parts:
  Part1 = Arduino Nano (Rev3.0)
  LCD = LCD-16X2 [package=lcd-16x2]
  IRSensor = Infrared Proximity Sensor
  Tranceiver = NRF24L01+ Breakout Board
  Pushbutton = Pushbutton [package="[THT]"]
  Battery = Battery block 9V
  OnOff = Toggle Switch [package=THT]
  R2 = Resistor [tolerance=±5% resistance=220 package=THT]
  R1 = Resistor [tolerance=±5% resistance=820 package=THT]

nets (from the breadboard view):
  GND: Part1.GND, LCD.VSS, LCD.R_W, LCD.K, IRSensor.GND, Tranceiver.GND, Battery.-, R2.Pin_0, R1.Pin_0
  N1: Part1.D2, LCD.RS
  N2: Part1.D3, LCD.E
  N3: Part1.D4, LCD.DB4
  N4: Part1.D5, LCD.DB5
  N5: Part1.D6, LCD.DB6
  N6: Part1.D7, LCD.DB7
  N7: Part1.D8, Pushbutton.Pin_1, Pushbutton.Pin_2, R2.Pin_1
  N8: Part1.D9, Tranceiver.CE
  N9: Part1.D10, Tranceiver.CS
  N10: Part1.D11/MOSI, Tranceiver.MOSI
  N11: Part1.D12/MISO, Tranceiver.MISO
  N12: Part1.VIN, OnOff.L1
  5V: Part1.5V, LCD.VDD, LCD.A, IRSensor.Vcc
  N13: Part1.A6, IRSensor.Vout
  3V3: Part1.3V3, Tranceiver.VCC, Pushbutton.Pin_3, Pushbutton.Pin_4
  N14: Part1.D13/SCK, Tranceiver.SCK
  N15: LCD.VO, R1.Pin_1
  N16: Battery.+, OnOff.COM
