# Fritzing sketch ArduinoMini_Photogate_Transmitter (saved by Fritzing 0.9.3b)
breadboards: 1

parts:
  Part1 = Arduino Nano (Rev3.0)
  IRSensor = Infrared Proximity Sensor
  tranceiver = NRF24L01+ Breakout Board
  PowerSwitch = Toggle Switch [package=THT]
  Button = Pushbutton [package="[THT]"]
  R1 = Resistor [tolerance=±5% resistance=220 package="1206 [SMD]"]
  Battery = Battery block 9V

nets:
  GND: Part1.GND, IRSensor.GND, tranceiver.GND, R1.Pin_0, Battery.-
  3V3: Part1.D7, Part1.3V3, tranceiver.VCC, Button.Pin_3, Button.Pin_4, R1.Pin_1
  N1: Part1.D9, tranceiver.CE
  N2: Part1.D10, tranceiver.CS
  N3: Part1.D11/MOSI, tranceiver.MOSI
  N4: Part1.D12/MISO, tranceiver.MISO
  N5: Part1.VIN, PowerSwitch.COM
  5V: Part1.5V, IRSensor.Vcc
  N6: Part1.A6, IRSensor.Vout
  N7: Part1.D13/SCK, tranceiver.SCK
  N8: PowerSwitch.L1, Battery.+
  N9: Button.Pin_1, Button.Pin_2
