# Fritzing sketch ArduinoNano_Photogate_Receiver (saved by Fritzing 0.9.3b)
circuit board: 4.99819cm x 5.87015cm
stripboards: 1
breadboards: 1

parts:
  Part1 = Arduino Nano (Rev3.0)
  LCD = LCD-16X2 [package=lcd-16x2]
  IRSensor = Infrared Proximity Sensor
  Tranceiver = NRF24L01+ Breakout Board
  Battery = Battery block 9V
  OnOff = Toggle Switch [package=THT]
  R1 = Resistor [tolerance=±5% resistance=820 package=THT]

nets:
  GND: Part1.GND, LCD.VSS, LCD.R_W, LCD.K, IRSensor.GND, Tranceiver.GND, Battery.-, R1.Pin_0
  N1: Part1.D2, LCD.RS
  N2: Part1.D3, LCD.E
  N3: Part1.D4, LCD.DB4
  N4: Part1.D5, LCD.DB5
  N5: Part1.D6, LCD.DB6
  N6: Part1.D7, LCD.DB7
  N7: Part1.D9, Tranceiver.CE
  N8: Part1.D10, Tranceiver.CS
  N9: Part1.D11/MOSI, Tranceiver.MOSI
  N10: Part1.D12/MISO, Tranceiver.MISO
  N11: Part1.VIN, Battery.+, OnOff.L1, OnOff.COM
  5V: Part1.5V, LCD.VDD, LCD.A, IRSensor.Vcc
  N12: Part1.A6, IRSensor.Vout
  3V3: Part1.3V3, Tranceiver.VCC
  N13: Part1.D13/SCK, Tranceiver.SCK
  N14: LCD.VO, R1.Pin_1
