# Fritzing sketch ArduinoNano_Photogate_Sender (saved by Fritzing 0.9.3b)
circuit board: 3.52994cm x 5.37276cm
breadboards: 1

parts:
  Part1 = Arduino Nano (Rev3.0)
  tranceiver = NRF24L01+ Breakout Board
  PowerSwitch = Toggle Switch [package=THT]
  Battery = Battery block 9V
  IRSensor = Infrared Proximity Sensor
  LED1 = LED - 5mm [color="Red (633nm)" package="5 mm [THT]"]
  R1 = Resistor [tolerance=±5% resistance=220 package=THT]

nets:
  GND: Part1.GND, tranceiver.GND, Battery.-, IRSensor.GND, R1.Pin_0
  N1: Part1.D2, LED1.cathode
  N2: Part1.D9, tranceiver.CE
  N3: Part1.D10, tranceiver.CS
  N4: Part1.D11/MOSI, tranceiver.MOSI
  N5: Part1.D12/MISO, tranceiver.MISO
  N6: Part1.VIN, PowerSwitch.COM
  5V: Part1.5V, IRSensor.Vcc
  N7: Part1.A6, IRSensor.Vout
  3V3: Part1.3V3, tranceiver.VCC
  N8: Part1.D13/SCK, tranceiver.SCK
  N9: PowerSwitch.L1, Battery.+
  N10: LED1.anode, R1.Pin_1
