# Fritzing sketch Beaglebone_PCBDesign (saved by Fritzing 0.9.3b)
perfboards: 1

parts:
  R1 = Slide Potentiometer [maximum_resistance=100kΩ]
  R2 = Slide Potentiometer [maximum_resistance=100kΩ]
  R3 = Slide Potentiometer [maximum_resistance=100kΩ]
  R4 = Slide Potentiometer [maximum_resistance=100kΩ]
  BeagleBone1 = BeagleBone Black
  3-Axis_Accelerometer1 = 3-Axis Accelerometer Breakout - MMA8452Q
  3-Axis_Accelerometer2 = 3-Axis Accelerometer Breakout - MMA8452Q
  Part1 = LSM303C (6 DOF)

nets:
  N1: R1.leg1, R2.leg1, R3.leg1, R4.leg1, BeagleBone1.no_name_yet#32
  N2: R1.wiper, BeagleBone1.no_name_yet#38
  N3: R1.leg2, R2.leg2, R3.leg2, R4.leg2, BeagleBone1.no_name_yet#34
  N4: R2.wiper, BeagleBone1.no_name_yet#37
  N5: R3.wiper, BeagleBone1.no_name_yet#40
  N6: R4.wiper, BeagleBone1.no_name_yet#39
  3.3V: 3-Axis_Accelerometer1.3.3V, 3-Axis_Accelerometer2.3.3V, Part1.VDD_IO
  GND: 3-Axis_Accelerometer1.GND, 3-Axis_Accelerometer2.GND, Part1.GND

custom parts:
  BeagleBone Black: BeagleBone Black rev. A5B
