# Fritzing sketch Beaglebone_PCBDesign_FritzingFile (saved by Fritzing 0.9.3b)
circuit board: 7.42801cm x 5.48902cm
breadboards: 1

parts:
  R1 = Slide Potentiometer [maximum_resistance=100kΩ]
  R2 = Slide Potentiometer [maximum_resistance=100kΩ]
  R3 = Slide Potentiometer [maximum_resistance=100kΩ]
  R4 = Slide Potentiometer [maximum_resistance=100kΩ]
  BeagleBone1 = BeagleBone Black

nets:
  N1: R1.leg1, R2.leg1, R3.leg1, R4.leg1, BeagleBone1.no_name_yet#34
  N2: R1.wiper, BeagleBone1.no_name_yet#39
  N3: R1.leg2, R2.leg2, R3.leg2, R4.leg2, BeagleBone1.no_name_yet#32
  N4: R2.wiper, BeagleBone1.no_name_yet#40
  N5: R3.wiper, BeagleBone1.no_name_yet#37
  N6: R4.wiper, BeagleBone1.no_name_yet#38

custom parts:
  BeagleBone Black: BeagleBone Black rev. A5B
